# Fritzing sketch AutomaticLightingSystem (saved by Fritzing 0.9.3b)
circuit board: 6.88566cm x 5.36311cm
breadboards: 1

parts:
  LED1 = LED - 5mm [color="White (6500K)" package="5 mm [THT]"]
  R1 = Resistor [tolerance=±5% resistance=220 package=THT]
  R2 = Resistor [tolerance=±5% resistance=220 package=THT]
  LED2 = LED - 5mm [color="White (6500K)" package="5 mm [THT]"]
  Photo_Resistor = Photocell (LDR) [package=THT]
  R3 = Resistor [tolerance=±5% resistance=100k package=THT]
  Bauteil1 = Arduino Uno (Rev3)
  S1 = SWITCH-MOMENTARY-2 [package=tactile-switch-1101ne]

nets (from the schematic view):
  N1: LED1.anode, LED2.anode, S1.2
  N2: R1.Pin_1, R2.Pin_1, Photo_Resistor.pin_0, Bauteil1.GND
  N3: R2.Pin_0, LED2.cathode
  N4: Photo_Resistor.pin_1, R3.Pin_0, Bauteil1.A0
  N5: R3.Pin_1, Bauteil1.5V
  N6: Bauteil1.D2, S1.1

notes:
  LIGHTING SYSTEM

// code stored in the sketch: AutomaticLightingSystem.ino
/*
  Automatic Lighting System
  schaltet die Lichter eines Autos ja nach Helligkeit an und ab
  
  Dieses Beispiel aus dem Fritzing Creator Kit: www.fritzing.org/creator-kit.
*/

int lichtsensorPin = 0;                            // lichtsensorPin wird deklariert
int scheinwerferPin = 2;                           // scheinwerferPin wird deklariert
int schaltgrenze = 300;                            // ab diesem Wert wird »Dunkelheit« definiert
int wartezeit = 1000;                              // Timer-Timeout sind 1000 Millisekunden
long timer = 0;                                    // Timervariabel wird deklariert
int lichtwert;                                     // speichert die Lichtsittuation

void setup(){
  Serial.begin(9600);                              // startet die serielle Kommunikation
  pinMode(scheinwerferPin,OUTPUT);                 // scheinwerferPin wird als OUTPUT initialisiert
}

void loop(){
  lichtwert = analogRead(lichtsensorPin);          // lichtwert wird eingelesen
  Serial.println(lichtwert);                       // lichtwert wird an die serielle Schnittstelle gesendet
  if (lichtwert>schaltgrenze){                     // wenn die Schaltgrenze unterschritten wird
    timer=millis();                                // timer wird auf aktuelle Zeit gesetzt
    digitalWrite(scheinwerferPin, HIGH);           // Scheinwerfer werden eingeschalten
  } else if (millis()>wartezeit+timer){            // sonst wenn er Timer abgelaufen ist
    digitalWrite(scheinwerferPin, LOW);            // werden die Scheinwerfer abgeschalten
  }
  delay(10);                                       // Pause
}
